// Digital circuit full_adder1.dig as structural Verilog
module full_adder1 (
  input  A,
  input  B,
  input  c_in,
  output Y,
  output C_out
);

  wire half_adder1_1_cout, half_adder1_1_sum, half_adder1_2_cout;

  half_adder1 half_adder1_1 (.B(A), .A(B), .sum(half_adder1_1_sum), .cout(half_adder1_1_cout));
  half_adder1 half_adder1_2 (.B(half_adder1_1_sum), .A(c_in), .sum(Y), .cout(half_adder1_2_cout));
  or1 or1_1 (.A(half_adder1_2_cout), .B(half_adder1_1_cout), .Y(C_out));
endmodule
