// Digital circuit half_adder1.dig as structural Verilog
module half_adder1 (
  input  B,
  input  A,
  output sum,
  output cout
);

  xor1 xor1_1 (.A(A), .B(B), .Y(sum));
  and1 and1_1 (.A(A), .B(B), .Y(cout));
endmodule
