// Digital circuit and1.dig as structural Verilog
module and1 (
  input  A,
  input  B,
  output Y
);

  wire nand_1_out;

  nand nand_1 (nand_1_out, A, B);
  not1 not1_1 (.A(nand_1_out), .Y(Y));
endmodule
