// Digital circuit or1.dig as structural Verilog
module or1 (
  input  A,
  input  B,
  output Y
);

  wire not1_1_y, not1_2_y;

  not1 not1_1 (.A(A), .Y(not1_1_y));
  not1 not1_2 (.A(B), .Y(not1_2_y));
  nand nand_1 (Y, not1_1_y, not1_2_y);
endmodule
