// Digital circuit xor1.dig as structural Verilog
module xor1 (
  input  A,
  input  B,
  output Y
);

  wire and1_1_y, and1_2_y, not1_1_y, not1_2_y;

  not1 not1_1 (.A(A), .Y(not1_1_y));
  not1 not1_2 (.A(B), .Y(not1_2_y));
  and1 and1_1 (.A(not1_1_y), .B(B), .Y(and1_1_y));
  and1 and1_2 (.A(A), .B(not1_2_y), .Y(and1_2_y));
  or1 or1_1 (.A(and1_1_y), .B(and1_2_y), .Y(Y));
endmodule
