// Digital circuit 16bit_computer.dig as structural Verilog
module _16bit_computer (
  input  [15:0] in,
  input  clk,
  input  reset
);

  wire cpu_1_m_w;
  wire [15:0] cpu_1_a_m, cpu_1_o_m, ram16k_1_out;

  cpu cpu_1 (
    .in(in), .in_m(ram16k_1_out), .r_set(reset), .clk(clk), .O_m(cpu_1_o_m), .m_w(cpu_1_m_w), .a_m(cpu_1_a_m));  // open: pc
  ram16k ram16k_1 (.data(cpu_1_o_m), .addr(cpu_1_a_m[13:0]), .load(cpu_1_m_w), .clk(clk), .out(ram16k_1_out));
endmodule
