// Digital circuit alu16.dig as structural Verilog
module alu16 (
  input  [15:0] a,
  input  [15:0] b,
  input  [2:0] op,
  output [15:0] out,
  output carry,
  output zero,
  output sign,
  output overflow
);

  wire add_1_c_o, and_2_out, and_3_out, and_4_out, and_5_out, and_6_out, and_7_out, and_8_out, and_9_out,
       and_10_out, and_11_out, and_12_out, and_13_out, and_14_out, and_15_out, and_16_out, and_17_out,
       and_18_out, and_19_out, and_20_out, and_21_out, and_22_out, and_23_out, and_24_out, and_25_out,
       and_26_out, and_27_out, and_28_out, and_29_out, and_30_out, and_31_out, and_32_out, and_33_out,
       multiplexer_5_out, multiplexer_6_out, multiplexer_9_out, multiplexer_10_out, shl16_1_c_out,
       shr16_1_c_out, sub_1_c_o, xnor_1_out, xor_2_out, xor_3_out, xor_4_out;
  wire [15:0] add_1_s, and_1_out, multiplexer_1_out, multiplexer_2_out, multiplexer_3_out, multiplexer_4_out,
       multiplexer_7_out, multiplexer_8_out, not_1_out, or_1_out, shl16_1_out, shr16_1_out, sub_1_s,
       xor_1_out;

  Add #(.Bits(16)) add_1 (.a(a), .b(b), .c_i(1'b0), .s(add_1_s), .c_o(add_1_c_o));
  Sub #(.Bits(16)) sub_1 (.a(a), .b(b), .c_i(1'b0), .s(sub_1_s), .c_o(sub_1_c_o));
  assign and_1_out = a & b;  // And and_1, 16 bits wide
  assign or_1_out = a | b;  // Or or_1, 16 bits wide
  assign xor_1_out = a ^ b;  // XOr xor_1, 16 bits wide
  assign not_1_out = ~a;  // Not not_1, 16 bits wide
  shl16 shl16_1 (.a(a), .c_out(shl16_1_c_out), .out(shl16_1_out));
  shr16 shr16_1 (.a(a), .c_out(shr16_1_c_out), .out(shr16_1_out));
  Multiplexer #(.Bits(16)) multiplexer_1 (.sel(op[0]), .in_0(add_1_s), .in_1(sub_1_s), .out(multiplexer_1_out));
  Multiplexer #(.Bits(16)) multiplexer_2 (.sel(op[0]), .in_0(and_1_out), .in_1(or_1_out), .out(multiplexer_2_out));
  Multiplexer #(.Bits(16)) multiplexer_3 (.sel(op[0]), .in_0(xor_1_out), .in_1(not_1_out), .out(multiplexer_3_out));
  Multiplexer #(.Bits(16)) multiplexer_4 (.sel(op[0]), .in_0(shl16_1_out), .in_1(shr16_1_out), .out(multiplexer_4_out));
  Multiplexer multiplexer_5 (.sel(op[0]), .in_0(add_1_c_o), .in_1(sub_1_c_o), .out(multiplexer_5_out));
  Multiplexer multiplexer_6 (.sel(op[0]), .in_0(shl16_1_c_out), .in_1(shr16_1_c_out), .out(multiplexer_6_out));
  Multiplexer #(.Bits(16)) multiplexer_7 (
    .sel(op[1]), .in_0(multiplexer_1_out), .in_1(multiplexer_2_out), .out(multiplexer_7_out));
  Multiplexer #(.Bits(16)) multiplexer_8 (
    .sel(op[1]), .in_0(multiplexer_3_out), .in_1(multiplexer_4_out), .out(multiplexer_8_out));
  Multiplexer multiplexer_9 (.sel(op[1]), .in_0(multiplexer_5_out), .in_1(1'b0), .out(multiplexer_9_out));
  Multiplexer multiplexer_10 (.sel(op[1]), .in_0(1'b0), .in_1(multiplexer_6_out), .out(multiplexer_10_out));
  Multiplexer #(.Bits(16)) multiplexer_11 (.sel(op[2]), .in_0(multiplexer_7_out), .in_1(multiplexer_8_out), .out(out));
  Multiplexer multiplexer_12 (.sel(op[2]), .in_0(multiplexer_9_out), .in_1(multiplexer_10_out), .out(carry));
  xnor xnor_1 (xnor_1_out, add_1_s[15], sub_1_s[15]);
  xor xor_2 (xor_2_out, add_1_s[15], out[15]);
  xor xor_3 (xor_3_out, add_1_s[15], sub_1_s[15]);
  xor xor_4 (xor_4_out, add_1_s[15], out[15]);
  and and_2 (and_2_out, xnor_1_out, xor_2_out);
  and and_3 (and_3_out, xor_3_out, xor_4_out);
  and and_4 (and_4_out, out[0], 1'b1);
  and and_5 (and_5_out, out[1], 1'b1);
  and and_6 (and_6_out, out[2], 1'b1);
  and and_7 (and_7_out, out[3], 1'b1);
  and and_8 (and_8_out, out[4], 1'b1);
  and and_9 (and_9_out, out[5], 1'b1);
  and and_10 (and_10_out, out[6], 1'b1);
  and and_11 (and_11_out, out[7], 1'b1);
  and and_12 (and_12_out, out[8], 1'b1);
  and and_13 (and_13_out, out[9], 1'b1);
  and and_14 (and_14_out, out[10], 1'b1);
  and and_15 (and_15_out, out[11], 1'b1);
  and and_16 (and_16_out, out[12], 1'b1);
  and and_17 (and_17_out, out[13], 1'b1);
  and and_18 (and_18_out, out[14], 1'b1);
  and and_19 (and_19_out, out[15], 1'b1);
  Multiplexer multiplexer_13 (.sel(op[0]), .in_0(and_2_out), .in_1(and_3_out), .out(overflow));
  and and_20 (and_20_out, and_4_out, and_5_out);
  and and_21 (and_21_out, and_6_out, and_7_out);
  and and_22 (and_22_out, and_8_out, and_9_out);
  and and_23 (and_23_out, and_10_out, and_11_out);
  and and_24 (and_24_out, and_12_out, and_13_out);
  and and_25 (and_25_out, and_14_out, and_15_out);
  and and_26 (and_26_out, and_16_out, and_17_out);
  and and_27 (and_27_out, and_18_out, and_19_out);
  and and_28 (and_28_out, and_20_out, and_21_out);
  and and_29 (and_29_out, and_22_out, and_23_out);
  and and_30 (and_30_out, and_24_out, and_25_out);
  and and_31 (and_31_out, and_26_out, and_27_out);
  and and_32 (and_32_out, and_28_out, and_29_out);
  and and_33 (and_33_out, and_30_out, and_31_out);
  and and_34 (zero, and_32_out, and_33_out);

  assign sign = out[15];
endmodule
