// Digital circuit cpu.dig as structural Verilog
module cpu (
  input  [15:0] in,
  input  [15:0] in_m,
  input  r_set,
  input  clk,
  output [15:0] O_m,
  output m_w,
  output [15:0] a_m,
  output [15:0] pc
);

  wire alu16_1_zero, instruction_decoder_1_alu_src, instruction_decoder_1_m2r, instruction_decoder_1_pc,
       instruction_decoder_1_rw, not_1_out;
  wire [2:0] instruction_decoder_1_op, instruction_decoder_1_rd, instruction_decoder_1_rs_a,
       instruction_decoder_1_rs_b;
  wire [15:0] alu16_1_out, instruction_decoder_1_im, multiplexer_1_out, multiplexer_2_out;

  instruction_decoder instruction_decoder_1 (
    .in(in), .zero(alu16_1_zero), .op(instruction_decoder_1_op), .rw(instruction_decoder_1_rw), .mw(m_w),
    .m2r(instruction_decoder_1_m2r), .alu_src(instruction_decoder_1_alu_src), .pc(instruction_decoder_1_pc),
    .rd(instruction_decoder_1_rd), .rs_A(instruction_decoder_1_rs_a), .rs_B(instruction_decoder_1_rs_b),
    .im(instruction_decoder_1_im));  // open: Unused
  registerfile registerfile_1 (
    .data(multiplexer_2_out), .addr(instruction_decoder_1_rd), .load(instruction_decoder_1_rw), .clk(clk),
    .r_A(instruction_decoder_1_rs_a), .r_b(instruction_decoder_1_rs_b), .O1(a_m), .O2(O_m));
  Multiplexer #(.Bits(16)) multiplexer_1 (
    .sel(instruction_decoder_1_alu_src), .in_0(O_m), .in_1(instruction_decoder_1_im), .out(multiplexer_1_out));
  alu16 alu16_1 (
    .a(a_m), .b(multiplexer_1_out), .op(instruction_decoder_1_op), .out(alu16_1_out), .zero(alu16_1_zero));  // open: carry, sign, overflow
  Multiplexer #(.Bits(16)) multiplexer_2 (
    .sel(instruction_decoder_1_m2r), .in_0(alu16_1_out), .in_1(in_m), .out(multiplexer_2_out));
  not not_1 (not_1_out, instruction_decoder_1_pc);
  program_counter program_counter_1 (
    .data(a_m), .inc(not_1_out), .reset(r_set), .load(instruction_decoder_1_pc), .clk(clk), .out(pc));
endmodule
