// Digital circuit instruction_decoder.dig as structural Verilog
module instruction_decoder (
  input  [15:0] in,
  input  zero,
  output [2:0] op,
  output rw,
  output mw,
  output m2r,
  output alu_src,
  output pc,
  output [2:0] rd,
  output [2:0] rs_A,
  output [2:0] rs_B,
  output [2:0] Unused,
  output [15:0] im
);

  wire and_1_out, and_2_out, and_3_out, and_4_out, and_5_out, and_6_out, and_7_out, and_8_out, and_9_out,
       and_10_out, and_14_out, and_15_out, and_16_out, not_1_out, not_2_out, not_3_out, not_4_out, not_5_out,
       not_6_out, not_7_out, not_8_out, not_9_out, not_10_out, not_11_out, or_1_out;

  not not_1 (not_1_out, in[15]);
  not not_2 (not_2_out, in[14]);
  not not_3 (not_3_out, in[13]);
  not not_4 (not_4_out, in[12]);
  not not_5 (not_5_out, in[14]);
  not not_6 (not_6_out, in[13]);
  not not_7 (not_7_out, in[14]);
  not not_8 (not_8_out, in[12]);
  not not_9 (not_9_out, in[14]);
  not not_10 (not_10_out, in[13]);
  not not_11 (not_11_out, in[12]);
  and and_1 (and_1_out, in[15], not_2_out);
  and and_2 (and_2_out, not_3_out, not_4_out);
  and and_3 (and_3_out, in[15], not_5_out);
  and and_4 (and_4_out, not_6_out, in[12]);
  and and_5 (and_5_out, in[15], not_7_out);
  and and_6 (and_6_out, in[13], not_8_out);
  and and_7 (and_7_out, in[15], not_9_out);
  and and_8 (and_8_out, in[13], in[12]);
  and and_9 (and_9_out, in[15], in[14]);
  and and_10 (and_10_out, not_10_out, not_11_out);
  and and_11 (alu_src, and_1_out, and_2_out);
  and and_12 (m2r, and_3_out, and_4_out);
  and and_13 (mw, and_5_out, and_6_out);
  and and_14 (and_14_out, and_7_out, and_8_out);
  and and_15 (and_15_out, and_9_out, and_10_out);
  or or_1 (or_1_out, not_1_out, alu_src);
  and and_16 (and_16_out, and_15_out, zero);
  or or_2 (rw, or_1_out, m2r);
  or or_3 (pc, and_14_out, and_16_out);

  assign im = {{7{1'b0}}, in[8:0]};
  assign op = in[14:12];
  assign rd = in[11:9];
  assign rs_A = in[8:6];
  assign rs_B = in[5:3];
  assign Unused = in[2:0];
endmodule
