// Digital circuit program_counter.dig as structural Verilog
module program_counter (
  input  [15:0] data,
  input  inc,
  input  reset,
  input  load,
  input  clk,
  output [15:0] out
);

  wire [15:0] add_1_s, multiplexer_1_out, multiplexer_2_out, multiplexer_3_out;

  Add #(.Bits(16)) add_1 (.a(out), .b({16{1'b0}}), .c_i(1'b1), .s(add_1_s));  // open: c_o
  Multiplexer #(.Bits(16)) multiplexer_1 (.sel(inc), .in_0(out), .in_1(add_1_s), .out(multiplexer_1_out));
  Multiplexer #(.Bits(16)) multiplexer_2 (.sel(load), .in_0(multiplexer_1_out), .in_1(data), .out(multiplexer_2_out));
  Multiplexer #(.Bits(16)) multiplexer_3 (
    .sel(reset), .in_0(multiplexer_2_out), .in_1({16{1'b0}}), .out(multiplexer_3_out));
  Register #(.Bits(16)) register_1 (.D(multiplexer_3_out), .C(clk), .en(1'b1), .Q(out));
endmodule
