// Digital circuit ram16k.dig as structural Verilog
module ram16k (
  input  [15:0] data,
  input  [13:0] addr,
  input  load,
  input  clk,
  output [15:0] out
);

  wire demultiplexer_1_out_0, demultiplexer_1_out_1, demultiplexer_1_out_2, demultiplexer_1_out_3;
  wire [15:0] ram4k_1_out, ram4k_2_out, ram4k_3_out, ram4k_4_out;

  Demultiplexer #(.Selector_Bits(2)) demultiplexer_1 (
    .sel(addr[1:0]), .in(load), .out_0(demultiplexer_1_out_0), .out_1(demultiplexer_1_out_1),
    .out_2(demultiplexer_1_out_2), .out_3(demultiplexer_1_out_3));
  ram4k ram4k_1 (.data(data), .addr(addr[13:2]), .load(demultiplexer_1_out_0), .clk(clk), .out(ram4k_1_out));
  ram4k ram4k_2 (.data(data), .addr(addr[13:2]), .load(demultiplexer_1_out_1), .clk(clk), .out(ram4k_2_out));
  ram4k ram4k_3 (.data(data), .addr(addr[13:2]), .load(demultiplexer_1_out_2), .clk(clk), .out(ram4k_3_out));
  ram4k ram4k_4 (.data(data), .addr(addr[13:2]), .load(demultiplexer_1_out_3), .clk(clk), .out(ram4k_4_out));
  Multiplexer #(.Selector_Bits(2), .Bits(16)) multiplexer_1 (
    .sel(addr[1:0]), .in_0(ram4k_1_out), .in_1(ram4k_2_out), .in_2(ram4k_3_out), .in_3(ram4k_4_out), .out(out));
endmodule
