// Digital circuit ram4k.dig as structural Verilog
module ram4k (
  input  [15:0] data,
  input  [11:0] addr,
  input  load,
  input  clk,
  output [15:0] out
);

  wire demultiplexer_1_out_0, demultiplexer_1_out_1, demultiplexer_1_out_2, demultiplexer_1_out_3,
       demultiplexer_1_out_4, demultiplexer_1_out_5, demultiplexer_1_out_6, demultiplexer_1_out_7;
  wire [15:0] ram512_1_out, ram512_2_out, ram512_3_out, ram512_4_out, ram512_5_out, ram512_6_out,
       ram512_7_out, ram512_8_out;

  Demultiplexer #(.Selector_Bits(3)) demultiplexer_1 (
    .sel(addr[2:0]), .in(load), .out_0(demultiplexer_1_out_0), .out_1(demultiplexer_1_out_1),
    .out_2(demultiplexer_1_out_2), .out_3(demultiplexer_1_out_3), .out_4(demultiplexer_1_out_4),
    .out_5(demultiplexer_1_out_5), .out_6(demultiplexer_1_out_6), .out_7(demultiplexer_1_out_7));
  ram512 ram512_1 (.data(data), .addr(addr[11:3]), .load(demultiplexer_1_out_0), .clk(clk), .out(ram512_1_out));
  ram512 ram512_2 (.data(data), .addr(addr[11:3]), .load(demultiplexer_1_out_1), .clk(clk), .out(ram512_2_out));
  ram512 ram512_3 (.data(data), .addr(addr[11:3]), .load(demultiplexer_1_out_2), .clk(clk), .out(ram512_3_out));
  ram512 ram512_4 (.data(data), .addr(addr[11:3]), .load(demultiplexer_1_out_3), .clk(clk), .out(ram512_4_out));
  ram512 ram512_5 (.data(data), .addr(addr[11:3]), .load(demultiplexer_1_out_4), .clk(clk), .out(ram512_5_out));
  ram512 ram512_6 (.data(data), .addr(addr[11:3]), .load(demultiplexer_1_out_5), .clk(clk), .out(ram512_6_out));
  ram512 ram512_7 (.data(data), .addr(addr[11:3]), .load(demultiplexer_1_out_6), .clk(clk), .out(ram512_7_out));
  ram512 ram512_8 (.data(data), .addr(addr[11:3]), .load(demultiplexer_1_out_7), .clk(clk), .out(ram512_8_out));
  Multiplexer #(.Selector_Bits(3), .Bits(16)) multiplexer_1 (
    .sel(addr[2:0]), .in_0(ram512_1_out), .in_1(ram512_2_out), .in_2(ram512_3_out), .in_3(ram512_4_out),
    .in_4(ram512_5_out), .in_5(ram512_6_out), .in_6(ram512_7_out), .in_7(ram512_8_out), .out(out));
endmodule
