// Digital circuit ram512.dig as structural Verilog
module ram512 (
  input  [15:0] data,
  input  [8:0] addr,
  input  load,
  input  clk,
  output [15:0] out
);

  wire demultiplexer_1_out_0, demultiplexer_1_out_1, demultiplexer_1_out_2, demultiplexer_1_out_3,
       demultiplexer_1_out_4, demultiplexer_1_out_5, demultiplexer_1_out_6, demultiplexer_1_out_7;
  wire [15:0] ram64_1_out, ram64_2_out, ram64_3_out, ram64_4_out, ram64_5_out, ram64_6_out, ram64_7_out,
       ram64_8_out;

  Demultiplexer #(.Selector_Bits(3)) demultiplexer_1 (
    .sel(addr[2:0]), .in(load), .out_0(demultiplexer_1_out_0), .out_1(demultiplexer_1_out_1),
    .out_2(demultiplexer_1_out_2), .out_3(demultiplexer_1_out_3), .out_4(demultiplexer_1_out_4),
    .out_5(demultiplexer_1_out_5), .out_6(demultiplexer_1_out_6), .out_7(demultiplexer_1_out_7));
  ram64 ram64_1 (.data(data), .addr(addr[8:3]), .load(demultiplexer_1_out_0), .clk(clk), .out(ram64_1_out));
  ram64 ram64_2 (.data(data), .addr(addr[8:3]), .load(demultiplexer_1_out_1), .clk(clk), .out(ram64_2_out));
  ram64 ram64_3 (.data(data), .addr(addr[8:3]), .load(demultiplexer_1_out_2), .clk(clk), .out(ram64_3_out));
  ram64 ram64_4 (.data(data), .addr(addr[8:3]), .load(demultiplexer_1_out_3), .clk(clk), .out(ram64_4_out));
  ram64 ram64_5 (.data(data), .addr(addr[8:3]), .load(demultiplexer_1_out_4), .clk(clk), .out(ram64_5_out));
  ram64 ram64_6 (.data(data), .addr(addr[8:3]), .load(demultiplexer_1_out_5), .clk(clk), .out(ram64_6_out));
  ram64 ram64_7 (.data(data), .addr(addr[8:3]), .load(demultiplexer_1_out_6), .clk(clk), .out(ram64_7_out));
  ram64 ram64_8 (.data(data), .addr(addr[8:3]), .load(demultiplexer_1_out_7), .clk(clk), .out(ram64_8_out));
  Multiplexer #(.Selector_Bits(3), .Bits(16)) multiplexer_1 (
    .sel(addr[2:0]), .in_0(ram64_1_out), .in_1(ram64_2_out), .in_2(ram64_3_out), .in_3(ram64_4_out),
    .in_4(ram64_5_out), .in_5(ram64_6_out), .in_6(ram64_7_out), .in_7(ram64_8_out), .out(out));
endmodule
