// Digital circuit ram64.dig as structural Verilog
module ram64 (
  input  [15:0] data,
  input  [5:0] addr,
  input  load,
  input  clk,
  output [15:0] out
);

  wire demultiplexer_1_out_0, demultiplexer_1_out_1, demultiplexer_1_out_2, demultiplexer_1_out_3,
       demultiplexer_1_out_4, demultiplexer_1_out_5, demultiplexer_1_out_6, demultiplexer_1_out_7;
  wire [15:0] ram8_1_out, ram8_2_out, ram8_3_out, ram8_4_out, ram8_5_out, ram8_6_out, ram8_7_out, ram8_8_out;

  Demultiplexer #(.Selector_Bits(3)) demultiplexer_1 (
    .sel(addr[2:0]), .in(load), .out_0(demultiplexer_1_out_0), .out_1(demultiplexer_1_out_1),
    .out_2(demultiplexer_1_out_2), .out_3(demultiplexer_1_out_3), .out_4(demultiplexer_1_out_4),
    .out_5(demultiplexer_1_out_5), .out_6(demultiplexer_1_out_6), .out_7(demultiplexer_1_out_7));
  ram8 ram8_1 (.data(data), .addr(addr[5:3]), .load(demultiplexer_1_out_0), .clk(clk), .out(ram8_1_out));
  ram8 ram8_2 (.data(data), .addr(addr[5:3]), .load(demultiplexer_1_out_1), .clk(clk), .out(ram8_2_out));
  ram8 ram8_3 (.data(data), .addr(addr[5:3]), .load(demultiplexer_1_out_2), .clk(clk), .out(ram8_3_out));
  ram8 ram8_4 (.data(data), .addr(addr[5:3]), .load(demultiplexer_1_out_3), .clk(clk), .out(ram8_4_out));
  ram8 ram8_5 (.data(data), .addr(addr[5:3]), .load(demultiplexer_1_out_4), .clk(clk), .out(ram8_5_out));
  ram8 ram8_6 (.data(data), .addr(addr[5:3]), .load(demultiplexer_1_out_5), .clk(clk), .out(ram8_6_out));
  ram8 ram8_7 (.data(data), .addr(addr[5:3]), .load(demultiplexer_1_out_6), .clk(clk), .out(ram8_7_out));
  ram8 ram8_8 (.data(data), .addr(addr[5:3]), .load(demultiplexer_1_out_7), .clk(clk), .out(ram8_8_out));
  Multiplexer #(.Selector_Bits(3), .Bits(16)) multiplexer_1 (
    .sel(addr[2:0]), .in_0(ram8_1_out), .in_1(ram8_2_out), .in_2(ram8_3_out), .in_3(ram8_4_out),
    .in_4(ram8_5_out), .in_5(ram8_6_out), .in_6(ram8_7_out), .in_7(ram8_8_out), .out(out));
endmodule
