// Digital circuit registerfile.dig as structural Verilog
module registerfile (
  input  [15:0] data,
  input  [2:0] addr,
  input  load,
  input  clk,
  input  [2:0] r_A,
  input  [2:0] r_b,
  output [15:0] O1,
  output [15:0] O2
);

  wire demultiplexer_1_out_0, demultiplexer_1_out_1, demultiplexer_1_out_2, demultiplexer_1_out_3,
       demultiplexer_1_out_4, demultiplexer_1_out_5, demultiplexer_1_out_6, demultiplexer_1_out_7;
  wire [15:0] register_1_q, register_2_q, register_3_q, register_4_q, register_5_q, register_6_q,
       register_7_q, register_8_q;

  Demultiplexer #(.Selector_Bits(3)) demultiplexer_1 (
    .sel(addr), .in(load), .out_0(demultiplexer_1_out_0), .out_1(demultiplexer_1_out_1),
    .out_2(demultiplexer_1_out_2), .out_3(demultiplexer_1_out_3), .out_4(demultiplexer_1_out_4),
    .out_5(demultiplexer_1_out_5), .out_6(demultiplexer_1_out_6), .out_7(demultiplexer_1_out_7));
  Register #(.Bits(16)) register_1 (.D(data), .C(clk), .en(demultiplexer_1_out_0), .Q(register_1_q));
  Register #(.Bits(16)) register_2 (.D(data), .C(clk), .en(demultiplexer_1_out_1), .Q(register_2_q));
  Register #(.Bits(16)) register_3 (.D(data), .C(clk), .en(demultiplexer_1_out_2), .Q(register_3_q));
  Register #(.Bits(16)) register_4 (.D(data), .C(clk), .en(demultiplexer_1_out_3), .Q(register_4_q));
  Register #(.Bits(16)) register_5 (.D(data), .C(clk), .en(demultiplexer_1_out_4), .Q(register_5_q));
  Register #(.Bits(16)) register_6 (.D(data), .C(clk), .en(demultiplexer_1_out_5), .Q(register_6_q));
  Register #(.Bits(16)) register_7 (.D(data), .C(clk), .en(demultiplexer_1_out_6), .Q(register_7_q));
  Register #(.Bits(16)) register_8 (.D(data), .C(clk), .en(demultiplexer_1_out_7), .Q(register_8_q));
  Multiplexer #(.Bits(16), .Selector_Bits(3)) multiplexer_1 (
    .sel(r_A), .in_0(register_1_q), .in_1(register_2_q), .in_2(register_3_q), .in_3(register_4_q),
    .in_4(register_5_q), .in_5(register_6_q), .in_6(register_7_q), .in_7(register_8_q), .out(O1));
  Multiplexer #(.Selector_Bits(3), .Bits(16)) multiplexer_2 (
    .sel(r_b), .in_0(register_1_q), .in_1(register_2_q), .in_2(register_3_q), .in_3(register_4_q),
    .in_4(register_5_q), .in_5(register_6_q), .in_6(register_7_q), .in_7(register_8_q), .out(O2));
endmodule
