// Logisim project 16bit_cpu.circ as structural Verilog
module nand_gate (
  input  a,
  input  b,
  output out1
);

  wire and_1_out;

  and and_1 (and_1_out, a, b);
  not not_1 (out1, and_1_out);
endmodule

module not_gate (
  input  a,
  output out1
);

  nand_gate nand_gate_1 (.a(a), .b(a), .out1(out1));
endmodule

module and_gate (
  input  a,
  input  b,
  output out1
);

  wire nand_gate_1_out1;

  nand_gate nand_gate_1 (.a(a), .b(b), .out1(nand_gate_1_out1));
  not_gate not_gate_1 (.a(nand_gate_1_out1), .out1(out1));
endmodule

module or_gate (
  input  in_1,
  input  in_2,
  output out_3
);

  wire not_gate_1_out1, not_gate_2_out1;

  not_gate not_gate_1 (.a(in_1), .out1(not_gate_1_out1));
  not_gate not_gate_2 (.a(in_2), .out1(not_gate_2_out1));
  nand_gate nand_gate_1 (.a(not_gate_1_out1), .b(not_gate_2_out1), .out1(out_3));
endmodule

module nor_gate (
  input  a,
  input  b,
  output out1
);

  wire or_gate_1_out_3;

  or_gate or_gate_1 (.in_1(a), .in_2(b), .out_3(or_gate_1_out_3));
  not_gate not_gate_1 (.a(or_gate_1_out_3), .out1(out1));
endmodule

module xor_gate (
  input  a,
  input  b,
  output out1
);

  wire nand_gate_1_out1, nand_gate_2_out1, nand_gate_3_out1;

  nand_gate nand_gate_1 (.a(a), .b(b), .out1(nand_gate_1_out1));
  nand_gate nand_gate_2 (.a(nand_gate_1_out1), .b(a), .out1(nand_gate_2_out1));
  nand_gate nand_gate_3 (.a(nand_gate_1_out1), .b(b), .out1(nand_gate_3_out1));
  nand_gate nand_gate_4 (.a(nand_gate_2_out1), .b(nand_gate_3_out1), .out1(out1));
endmodule

module xnor_gate (
  input  a,
  input  b,
  output out1
);

  wire xor_gate_1_out1;

  xor_gate xor_gate_1 (.a(a), .b(b), .out1(xor_gate_1_out1));
  not_gate not_gate_1 (.a(xor_gate_1_out1), .out1(out1));
endmodule

module half_adder (
  input  a,
  input  b,
  output sum,
  output carry
);

  xor_gate xor_gate_1 (.a(a), .b(b), .out1(sum));
  and_gate and_gate_1 (.a(a), .b(b), .out1(carry));
endmodule

module full_adder (
  input  a,
  input  b,
  input  cin,
  output sum,
  output carry
);

  wire half_adder_1_carry, half_adder_1_sum, half_adder_2_carry;

  half_adder half_adder_1 (.a(a), .b(b), .sum(half_adder_1_sum), .carry(half_adder_1_carry));
  half_adder half_adder_2 (.a(half_adder_1_sum), .b(cin), .sum(sum), .carry(half_adder_2_carry));
  or or_1 (carry, half_adder_2_carry, half_adder_1_carry);
endmodule

module mux (
  input  a,
  input  b,
  input  sel,
  output out1
);

  wire and_1_out, and_2_out, not_1_out;

  not not_1 (not_1_out, sel);
  and and_1 (and_1_out, a, not_1_out);
  and and_2 (and_2_out, b, sel);
  or or_1 (out1, and_1_out, and_2_out);
endmodule

module mux4way16 (
  input  [1:0] sel,
  input  [15:0] a,
  input  [15:0] b,
  input  [15:0] c,
  input  [15:0] d,
  output [15:0] out1
);

  wire [15:0] mux16_1_out_4, mux16_2_out_4;

  mux16 mux16_1 (.sel(sel[0]), .a(a), .b(b), .out_4(mux16_1_out_4));
  mux16 mux16_2 (.sel(sel[0]), .a(c), .b(d), .out_4(mux16_2_out_4));
  mux16 mux16_3 (.sel(sel[1]), .a(mux16_1_out_4), .b(mux16_2_out_4), .out_4(out1));
endmodule

module mux16 (
  input  sel,
  input  [15:0] a,
  input  [15:0] b,
  output [15:0] out_4
);

  mux mux_1 (.a(a[0]), .b(b[0]), .sel(sel), .out1(out_4[0]));
  mux mux_2 (.a(a[1]), .b(b[1]), .sel(sel), .out1(out_4[1]));
  mux mux_3 (.a(a[2]), .b(b[2]), .sel(sel), .out1(out_4[2]));
  mux mux_4 (.a(a[3]), .b(b[3]), .sel(sel), .out1(out_4[3]));
  mux mux_5 (.a(a[4]), .b(b[4]), .sel(sel), .out1(out_4[4]));
  mux mux_6 (.a(a[5]), .b(b[5]), .sel(sel), .out1(out_4[5]));
  mux mux_7 (.a(a[6]), .b(b[6]), .sel(sel), .out1(out_4[6]));
  mux mux_8 (.a(a[7]), .b(b[7]), .sel(sel), .out1(out_4[7]));
  mux mux_9 (.a(a[8]), .b(b[8]), .sel(sel), .out1(out_4[8]));
  mux mux_10 (.a(a[9]), .b(b[9]), .sel(sel), .out1(out_4[9]));
  mux mux_11 (.a(a[10]), .b(b[10]), .sel(sel), .out1(out_4[10]));
  mux mux_12 (.a(a[11]), .b(b[11]), .sel(sel), .out1(out_4[11]));
  mux mux_13 (.a(a[12]), .b(b[12]), .sel(sel), .out1(out_4[12]));
  mux mux_14 (.a(a[13]), .b(b[13]), .sel(sel), .out1(out_4[13]));
  mux mux_15 (.a(a[14]), .b(b[14]), .sel(sel), .out1(out_4[14]));
  mux mux_16 (.a(a[15]), .b(b[15]), .sel(sel), .out1(out_4[15]));
endmodule

module mux8way16 (
  input  [2:0] sel,
  input  [15:0] a,
  input  [15:0] b,
  input  [15:0] c,
  input  [15:0] d,
  input  [15:0] e,
  input  [15:0] f,
  input  [15:0] g,
  input  [15:0] h,
  output [15:0] out1
);

  wire [15:0] mux16_1_out_4, mux16_2_out_4, mux16_3_out_4, mux16_4_out_4, mux16_5_out_4, mux16_6_out_4;

  mux16 mux16_1 (.sel(sel[0]), .a(a), .b(b), .out_4(mux16_1_out_4));
  mux16 mux16_2 (.sel(sel[0]), .a(c), .b(d), .out_4(mux16_2_out_4));
  mux16 mux16_3 (.sel(sel[0]), .a(e), .b(f), .out_4(mux16_3_out_4));
  mux16 mux16_4 (.sel(sel[0]), .a(g), .b(h), .out_4(mux16_4_out_4));
  mux16 mux16_5 (.sel(sel[1]), .a(mux16_1_out_4), .b(mux16_2_out_4), .out_4(mux16_5_out_4));
  mux16 mux16_6 (.sel(sel[1]), .a(mux16_3_out_4), .b(mux16_4_out_4), .out_4(mux16_6_out_4));
  mux16 mux16_7 (.sel(sel[2]), .a(mux16_5_out_4), .b(mux16_6_out_4), .out_4(out1));
endmodule

module dmux (
  input  sel,
  input  in1,
  output out1,
  output out2
);

  wire not_1_out;

  not not_1 (not_1_out, sel);
  and and_1 (out1, in1, not_1_out);
  and and_2 (out2, in1, sel);
endmodule

module dmux4way (
  input  [1:0] sel,
  input  in1,
  output out1,
  output out2,
  output out3,
  output out4
);

  wire dmux_1_out1, dmux_1_out2;

  dmux dmux_1 (.sel(sel[1]), .in1(in1), .out1(dmux_1_out1), .out2(dmux_1_out2));
  dmux dmux_2 (.sel(sel[0]), .in1(dmux_1_out1), .out1(out1), .out2(out2));
  dmux dmux_3 (.sel(sel[0]), .in1(dmux_1_out2), .out1(out3), .out2(out4));
endmodule

module dmux8way (
  input  [2:0] sel,
  input  in1,
  output out1,
  output out2,
  output out3,
  output out4,
  output out5,
  output out6,
  output out7,
  output out8
);

  wire dmux_1_out1, dmux_1_out2, dmux_2_out1, dmux_2_out2, dmux_3_out1, dmux_3_out2;

  dmux dmux_1 (.sel(sel[2]), .in1(in1), .out1(dmux_1_out1), .out2(dmux_1_out2));
  dmux dmux_2 (.sel(sel[1]), .in1(dmux_1_out1), .out1(dmux_2_out1), .out2(dmux_2_out2));
  dmux dmux_3 (.sel(sel[1]), .in1(dmux_1_out2), .out1(dmux_3_out1), .out2(dmux_3_out2));
  dmux dmux_4 (.sel(sel[0]), .in1(dmux_2_out1), .out1(out1), .out2(out2));
  dmux dmux_5 (.sel(sel[0]), .in1(dmux_2_out2), .out1(out3), .out2(out4));
  dmux dmux_6 (.sel(sel[0]), .in1(dmux_3_out1), .out1(out5), .out2(out6));
  dmux dmux_7 (.sel(sel[0]), .in1(dmux_3_out2), .out1(out7), .out2(out8));
endmodule

module not16 (
  input  [15:0] a,
  output [15:0] out1
);

  not_gate not_gate_1 (.a(a[0]), .out1(out1[0]));
  not_gate not_gate_2 (.a(a[1]), .out1(out1[1]));
  not_gate not_gate_3 (.a(a[2]), .out1(out1[2]));
  not_gate not_gate_4 (.a(a[3]), .out1(out1[3]));
  not_gate not_gate_5 (.a(a[4]), .out1(out1[4]));
  not_gate not_gate_6 (.a(a[5]), .out1(out1[5]));
  not_gate not_gate_7 (.a(a[6]), .out1(out1[6]));
  not_gate not_gate_8 (.a(a[7]), .out1(out1[7]));
  not_gate not_gate_9 (.a(a[8]), .out1(out1[8]));
  not_gate not_gate_10 (.a(a[9]), .out1(out1[9]));
  not_gate not_gate_11 (.a(a[10]), .out1(out1[10]));
  not_gate not_gate_12 (.a(a[11]), .out1(out1[11]));
  not_gate not_gate_13 (.a(a[12]), .out1(out1[12]));
  not_gate not_gate_14 (.a(a[13]), .out1(out1[13]));
  not_gate not_gate_15 (.a(a[14]), .out1(out1[14]));
  not_gate not_gate_16 (.a(a[15]), .out1(out1[15]));
endmodule

module and16 (
  input  [15:0] a,
  input  [15:0] b,
  output [15:0] out1
);

  and_gate and_gate_1 (.a(a[0]), .b(b[0]), .out1(out1[0]));
  and_gate and_gate_2 (.a(a[1]), .b(b[1]), .out1(out1[1]));
  and_gate and_gate_3 (.a(a[2]), .b(b[2]), .out1(out1[2]));
  and_gate and_gate_4 (.a(a[3]), .b(b[3]), .out1(out1[3]));
  and_gate and_gate_5 (.a(a[4]), .b(b[4]), .out1(out1[4]));
  and_gate and_gate_6 (.a(a[5]), .b(b[5]), .out1(out1[5]));
  and_gate and_gate_7 (.a(a[6]), .b(b[6]), .out1(out1[6]));
  and_gate and_gate_8 (.a(a[7]), .b(b[7]), .out1(out1[7]));
  and_gate and_gate_9 (.a(a[8]), .b(b[8]), .out1(out1[8]));
  and_gate and_gate_10 (.a(a[9]), .b(b[9]), .out1(out1[9]));
  and_gate and_gate_11 (.a(a[10]), .b(b[10]), .out1(out1[10]));
  and_gate and_gate_12 (.a(a[11]), .b(b[11]), .out1(out1[11]));
  and_gate and_gate_13 (.a(a[12]), .b(b[12]), .out1(out1[12]));
  and_gate and_gate_14 (.a(a[13]), .b(b[13]), .out1(out1[13]));
  and_gate and_gate_15 (.a(a[14]), .b(b[14]), .out1(out1[14]));
  and_gate and_gate_16 (.a(a[15]), .b(b[15]), .out1(out1[15]));
endmodule

module or16 (
  input  [15:0] a,
  input  [15:0] b,
  output [15:0] out1
);

  or_gate or_gate_1 (.in_1(a[0]), .in_2(b[0]), .out_3(out1[0]));
  or_gate or_gate_2 (.in_1(a[1]), .in_2(b[1]), .out_3(out1[1]));
  or_gate or_gate_3 (.in_1(a[2]), .in_2(b[2]), .out_3(out1[2]));
  or_gate or_gate_4 (.in_1(a[3]), .in_2(b[3]), .out_3(out1[3]));
  or_gate or_gate_5 (.in_1(a[4]), .in_2(b[4]), .out_3(out1[4]));
  or_gate or_gate_6 (.in_1(a[5]), .in_2(b[5]), .out_3(out1[5]));
  or_gate or_gate_7 (.in_1(a[6]), .in_2(b[6]), .out_3(out1[6]));
  or_gate or_gate_8 (.in_1(a[7]), .in_2(b[7]), .out_3(out1[7]));
  or_gate or_gate_9 (.in_1(a[8]), .in_2(b[8]), .out_3(out1[8]));
  or_gate or_gate_10 (.in_1(a[9]), .in_2(b[9]), .out_3(out1[9]));
  or_gate or_gate_11 (.in_1(a[10]), .in_2(b[10]), .out_3(out1[10]));
  or_gate or_gate_12 (.in_1(a[11]), .in_2(b[11]), .out_3(out1[11]));
  or_gate or_gate_13 (.in_1(a[12]), .in_2(b[12]), .out_3(out1[12]));
  or_gate or_gate_14 (.in_1(a[13]), .in_2(b[13]), .out_3(out1[13]));
  or_gate or_gate_15 (.in_1(a[14]), .in_2(b[14]), .out_3(out1[14]));
  or_gate or_gate_16 (.in_1(a[15]), .in_2(b[15]), .out_3(out1[15]));
endmodule

module xor16 (
  input  [15:0] a,
  input  [15:0] b,
  output [15:0] out1
);

  xor_gate xor_gate_1 (.a(a[0]), .b(b[0]), .out1(out1[0]));
  xor_gate xor_gate_2 (.a(a[1]), .b(b[1]), .out1(out1[1]));
  xor_gate xor_gate_3 (.a(a[2]), .b(b[2]), .out1(out1[2]));
  xor_gate xor_gate_4 (.a(a[3]), .b(b[3]), .out1(out1[3]));
  xor_gate xor_gate_5 (.a(a[4]), .b(b[4]), .out1(out1[4]));
  xor_gate xor_gate_6 (.a(a[5]), .b(b[5]), .out1(out1[5]));
  xor_gate xor_gate_7 (.a(a[6]), .b(b[6]), .out1(out1[6]));
  xor_gate xor_gate_8 (.a(a[7]), .b(b[7]), .out1(out1[7]));
  xor_gate xor_gate_9 (.a(a[8]), .b(b[8]), .out1(out1[8]));
  xor_gate xor_gate_10 (.a(a[9]), .b(b[9]), .out1(out1[9]));
  xor_gate xor_gate_11 (.a(a[10]), .b(b[10]), .out1(out1[10]));
  xor_gate xor_gate_12 (.a(a[11]), .b(b[11]), .out1(out1[11]));
  xor_gate xor_gate_13 (.a(a[12]), .b(b[12]), .out1(out1[12]));
  xor_gate xor_gate_14 (.a(a[13]), .b(b[13]), .out1(out1[13]));
  xor_gate xor_gate_15 (.a(a[14]), .b(b[14]), .out1(out1[14]));
  xor_gate xor_gate_16 (.a(a[15]), .b(b[15]), .out1(out1[15]));
endmodule

module add16 (
  input  [15:0] a,
  input  [15:0] b,
  output [15:0] out1,
  output carry
);

  wire full_adder_1_carry, full_adder_2_carry, full_adder_3_carry, full_adder_4_carry, full_adder_5_carry,
       full_adder_6_carry, full_adder_7_carry, full_adder_8_carry, full_adder_9_carry, full_adder_10_carry,
       full_adder_11_carry, full_adder_12_carry, full_adder_13_carry, full_adder_14_carry,
       full_adder_15_carry, undriven, undriven_2;

  full_adder full_adder_1 (.a(a[0]), .b(b[0]), .cin(1'b0), .carry(full_adder_1_carry));  // open: sum
  full_adder full_adder_2 (.a(a[1]), .b(b[1]), .cin(full_adder_1_carry), .carry(full_adder_2_carry));  // open: sum
  full_adder full_adder_3 (.a(a[2]), .b(b[2]), .cin(full_adder_2_carry), .carry(full_adder_3_carry));  // open: sum
  full_adder full_adder_4 (.a(a[3]), .b(b[3]), .cin(full_adder_3_carry), .carry(full_adder_4_carry));  // open: sum
  full_adder full_adder_5 (.a(a[4]), .b(b[4]), .cin(full_adder_4_carry), .carry(full_adder_5_carry));  // open: sum
  full_adder full_adder_6 (.a(a[5]), .b(b[5]), .cin(full_adder_5_carry), .carry(full_adder_6_carry));  // open: sum
  full_adder full_adder_7 (.a(a[6]), .b(b[6]), .cin(full_adder_6_carry), .carry(full_adder_7_carry));  // open: sum
  full_adder full_adder_8 (
    .a(undriven), .b(undriven_2), .cin(full_adder_7_carry), .carry(full_adder_8_carry));  // open: sum
  full_adder full_adder_9 (.cin(full_adder_8_carry), .carry(full_adder_9_carry));  // open: a, b, sum
  full_adder full_adder_10 (.cin(full_adder_9_carry), .carry(full_adder_10_carry));  // open: a, b, sum
  full_adder full_adder_11 (.cin(full_adder_10_carry), .carry(full_adder_11_carry));  // open: a, b, sum
  full_adder full_adder_12 (.cin(full_adder_11_carry), .carry(full_adder_12_carry));  // open: a, b, sum
  full_adder full_adder_13 (.cin(full_adder_12_carry), .carry(full_adder_13_carry));  // open: a, b, sum
  full_adder full_adder_14 (.cin(full_adder_13_carry), .carry(full_adder_14_carry));  // open: a, b, sum
  full_adder full_adder_15 (.cin(full_adder_14_carry), .carry(full_adder_15_carry));  // open: a, b, sum
  full_adder full_adder_16 (.cin(full_adder_15_carry), .carry(carry));  // open: a, b, sum
endmodule
